// Logisim project MIPS32.circ as structural Verilog: 7 circuits, main circuit main
module main (
);

  wire and_1_out, C, comparator_1_lt, comparator_2_lt, control_1_movn, control_1_mux1, control_1_mux2,
       control_1_mux3, control_1_mux4, control_1_sa, control_1_sltumux, control_1_we, mipsprogramrom_1_p3,
       MOVN_q, multiplexer_8_out, Mux1_q, Mux2_q, Mux3_q, or_1_out, registerfile_1_p2, Sa_q, SLTUMux_q,
       WE1_q, WE_q, xor_1_out;
  wire [1:0] FA, FB;
  wire [3:0] control_1_aluop, Op_q;
  wire [4:0] control_1_ra, control_1_rb, control_1_rw, control_1_shamt, mips_alu_1_p4, multiplexer_2_out,
       rA1_q, rA3_q, rA_q, rB1_q, rB2_q, rB_q, registerfile_1_p3, rW2_q, rW_q, Shamt_q;
  wire [26:0] multiplexer_2_out_2;
  wire [29:0] PC_q_2;
  wire [31:0] A_q, B_q, bit_extender_1_out, bit_extender_2_out, bit_extender_3_out, bit_extender_4_out, D_q,
       Imm_q, incrementer_1_p3, mips_alu_1_p5, mipsprogramrom_1_p2, multiplexer_1_out, multiplexer_3_out,
       multiplexer_4_out, multiplexer_6_out, multiplexer_7_out, PC_q, registerfile_1_p1, registerfile_1_p6,
       registerfile_1_p7;

  Clock clock_1 (.out(C));
  Register #(.width(32)) PC (.D(PC_q), .clk(C), .Q({PC_q_2, PC_q[1:0]}));  // open: en, clr
  // Incrementer #(.width(30)) incrementer_1: pin names not known; wires that end beside it: PC_q_2, PC_q[31:2], incrementer_1_p3
  Register #(.width(32)) Inst (
    .D(mipsprogramrom_1_p2), .en(mipsprogramrom_1_p3), .clk(C), .Q(incrementer_1_p3));  // open: clr
  // MIPSProgramROM mipsprogramrom_1: pin names not known; wires that end beside it: {PC_q_2, PC_q[1:0]}, mipsprogramrom_1_p2, mipsprogramrom_1_p3, C
  control control_1 (
    .Inst(incrementer_1_p3), .AluOp(control_1_aluop), .MOVN(control_1_movn), .Sa(control_1_sa),
    .Shamt(control_1_shamt), .rA(control_1_ra), .Mux3(control_1_mux3), .rB(control_1_rb), .rW(control_1_rw),
    .WE(control_1_we), .Mux1(control_1_mux1), .Mux2(control_1_mux2), .Mux4(control_1_mux4),
    .SLTUMux(control_1_sltumux));
  Register #(.width(1)) SLTUMux (.D(control_1_sltumux), .clk(C), .Q(SLTUMux_q));  // open: en, clr
  assign bit_extender_1_out = {{16{incrementer_1_p3[15]}}, incrementer_1_p3[15:0]};  // Bit_Extender bit_extender_1
  assign bit_extender_2_out = {{16{1'b0}}, incrementer_1_p3[15:0]};  // Bit_Extender bit_extender_2
  // RegisterFile #(.trigger("falling")) registerfile_1: pin names not known; wires that end beside it: registerfile_1_p1, registerfile_1_p2, registerfile_1_p3, control_1_ra, control_1_rb, registerfile_1_p6, registerfile_1_p7
  Multiplexer #(.width(32), .enable("false")) multiplexer_1 (
    .in0(bit_extender_1_out), .in1(bit_extender_2_out), .out(multiplexer_1_out), .sel(control_1_mux4));
  Register #(.width(32)) A (.D(registerfile_1_p6), .clk(C), .Q(A_q));  // open: en, clr
  Register #(.width(32)) B (.D(registerfile_1_p7), .clk(C), .Q(B_q));  // open: en, clr
  Register #(.width(1)) Mux1 (.D(control_1_mux1), .clk(C), .Q(Mux1_q));  // open: en, clr
  Register #(.width(4)) Op (.D(control_1_aluop), .clk(C), .Q(Op_q));  // open: en, clr
  Register #(.width(5)) Shamt (.D(control_1_shamt), .clk(C), .Q(Shamt_q));  // open: en, clr
  Register #(.width(1)) WE (.D(control_1_we), .clk(C), .Q(WE_q));  // open: en, clr
  Register #(.width(5)) rW (.D(control_1_rw), .clk(C), .Q(rW_q));  // open: en, clr
  Register #(.width(5)) rA (.D(control_1_ra), .clk(C), .Q(rA_q));  // open: en, clr
  Register #(.width(5)) rB (.D(control_1_rb), .clk(C), .Q(rB_q));  // open: en, clr
  Register #(.width(32)) Imm (.D(multiplexer_1_out), .clk(C), .Q(Imm_q));  // open: en, clr
  Register #(.width(1)) Sa (.D(control_1_sa), .clk(C), .Q(Sa_q));  // open: en, clr
  Register #(.width(1)) Mux2 (.D(control_1_mux2), .clk(C), .Q(Mux2_q));  // open: en, clr
  Register #(.width(1)) Mux3 (.D(control_1_mux3), .clk(C), .Q(Mux3_q));  // open: en, clr
  Register #(.width(1)) MOVN (.D(control_1_movn), .clk(C), .Q(MOVN_q));  // open: en, clr
  Multiplexer #(.select(2), .width(32), .enable("false")) multiplexer_2 (
    .in0(A_q), .in1(registerfile_1_p1), .in2(D_q), .out({multiplexer_2_out_2, multiplexer_2_out}), .sel(FA));  // open: in3
  Multiplexer #(.select(2), .width(32), .enable("false")) multiplexer_3 (
    .in0(B_q), .in1(registerfile_1_p1), .in2(D_q), .out(multiplexer_3_out), .sel(FB));  // open: in3
  Multiplexer #(.width(32), .enable("false")) multiplexer_4 (
    .in0(multiplexer_3_out), .in1(Imm_q), .out(multiplexer_4_out), .sel(Mux1_q));
  // Mips_ALU mips_alu_1: pin names not known; wires that end beside it: {multiplexer_2_out_2, multiplexer_2_out}, multiplexer_4_out, Op_q, mips_alu_1_p4, mips_alu_1_p5
  Comparator #(.width(32)) comparator_1 (
    .a({multiplexer_2_out_2, multiplexer_2_out}), .b(multiplexer_4_out), .lt(comparator_1_lt));  // open: gt, eq
  Comparator #(.width(32), .mode("unsigned")) comparator_2 (
    .a({multiplexer_2_out_2, multiplexer_2_out}), .b(multiplexer_4_out), .lt(comparator_2_lt));  // open: gt, eq
  Multiplexer #(.width(5), .enable("false")) multiplexer_5 (
    .in0(multiplexer_2_out), .in1(Shamt_q), .out(mips_alu_1_p4), .sel(Sa_q));
  assign bit_extender_3_out = {{31{1'b0}}, comparator_1_lt};  // Bit_Extender bit_extender_3
  assign bit_extender_4_out = {{31{1'b0}}, comparator_2_lt};  // Bit_Extender bit_extender_4
  or or_1 (or_1_out, multiplexer_2_out[0], multiplexer_2_out[1], multiplexer_2_out[2], multiplexer_2_out[3], multiplexer_2_out[4], multiplexer_2_out_2[0], multiplexer_2_out_2[1], multiplexer_2_out_2[2], multiplexer_2_out_2[3], multiplexer_2_out_2[4], multiplexer_2_out_2[5], multiplexer_2_out_2[6], multiplexer_2_out_2[7], multiplexer_2_out_2[8], multiplexer_2_out_2[9], multiplexer_2_out_2[10], multiplexer_2_out_2[12], multiplexer_2_out_2[13], multiplexer_2_out_2[14], multiplexer_2_out_2[15], multiplexer_2_out_2[16], multiplexer_2_out_2[17], multiplexer_2_out_2[18], multiplexer_2_out_2[19], multiplexer_2_out_2[20], multiplexer_2_out_2[21], multiplexer_2_out_2[22], multiplexer_2_out_2[23], multiplexer_2_out_2[24], multiplexer_2_out_2[25], multiplexer_2_out_2[26], multiplexer_2_out_2[11]);
  Multiplexer #(.width(32), .enable("false")) multiplexer_6 (
    .in0(bit_extender_3_out), .in1(bit_extender_4_out), .out(multiplexer_6_out), .sel(SLTUMux_q));
  xor xor_1 (xor_1_out, or_1_out, MOVN_q);
  Multiplexer #(.width(32), .enable("false")) multiplexer_7 (
    .in0(mips_alu_1_p5), .in1(multiplexer_6_out), .out(multiplexer_7_out), .sel(Mux2_q));
  and and_1 (and_1_out, xor_1_out, WE_q);
  Register #(.width(32)) D (.D(multiplexer_7_out), .clk(C), .Q(D_q));  // open: en, clr
  Register #(.width(5)) rW2 (.D(rW_q), .en(C), .clk(C), .Q(rW2_q));  // open: clr
  Register #(.width(1)) WE1 (.D(multiplexer_8_out), .clk(C), .Q(WE1_q));  // open: en, clr
  Multiplexer #(.enable("false")) multiplexer_8 (.in0(WE_q), .in1(and_1_out), .out(multiplexer_8_out), .sel(Mux3_q));
  Register #(.width(5)) rB1 (.D(rB_q), .clk(C), .Q(rB1_q));  // open: en, clr
  Register #(.width(5)) rA1 (.D(rA_q), .clk(C), .Q(rA1_q));  // open: en, clr
  Register #(.width(32)) D1 (.D(D_q), .clk(C), .Q(registerfile_1_p1));  // open: en, clr
  Register #(.width(5)) rW3 (.D(rW2_q), .clk(C), .Q(registerfile_1_p3));  // open: en, clr
  Register #(.width(1)) WE2 (.D(WE1_q), .clk(C), .Q(registerfile_1_p2));  // open: en, clr
  Register #(.width(5)) rB2 (.D(rB1_q), .clk(C), .Q(rB2_q));  // open: en, clr
  Register #(.width(5)) rA3 (.D(rA1_q), .clk(C), .Q(rA3_q));  // open: en, clr
  Forwarding forwarding_1 (
    .IDEXRb(rB_q), .EXMEMrA(rA1_q), .EXMEMrW(rW2_q), .EXMEMrB(rB1_q), .IDEXRa(rA_q),
    .MEMWBrW(registerfile_1_p3), .IDEXrW(rW_q), .EXMEMWE(WE1_q), .IDEXWE(multiplexer_8_out),
    .MEMWBWE(registerfile_1_p2), .MEMWBrA(rA3_q), .MEMWBrB(rB2_q), .ForwardA(FA), .ForwardB(FB));

  // Notes on the sheet:
  //   contents of mipsprogramrom_1 (hex, n*v repeats v):
  //   SLLV $15, $24, $27 SLTI $16, $17, -31417 SLTI $19, $27, -5575 MOVZ $12, $2, $27 SLTIU $27, $3, 7593
  //   SRA $6, $14, 15 LUI $0, 65535 LUI $19, 39346 SLL $8, $25, 28 MOVN $0, $12, $10 ORI $28, $5, 56948
  //   MOVN $5, $4, $13 AND $21, $15, $3 LUI $31, 0 SLLV $7, $4, $22 SRL $31, $16, 10 SLT $4, $0, $21 AND
  //   $20, $1, $8 ADDIU $2, $31, 15461 LUI $31, 65535 LUI $29, 22549 SRLV $27, $19, $17 SRL $30, $1, 27
  //   ADDU $11, $14, $1 ADDIU $0, $0, -32768 AND $17, $16, $4 ANDI $21, $6, 9482 MOVZ $27, $23, $30 ORI
  //   $25, $31, 11779 SRL $31, $21, 18 MOVN $25, $11, $15 SRL $2, $18, 31 SLTI $6, $17, 2091 ADDIU $0, $0,
  //   32767 SRA $7, $22, 31 ADDU $19, $4, $23 SLTU $29, $28, $26 XORI $11, $30, 41976 SLL $29, $30, 12
  //   ANDI $18, $29, 7232 ADDIU $0, $31, -32768 MOVN $14, $26, $19 NOR $23, $23, $2 LUI $13, 37784 SLL
  //   $31, $20, 17 ADDIU $0, $31, 32767 SLTU $31, $23, $10 ADDIU $20, $16, -24251 LUI $2, 38252 SLLV $18,
  //   $11, $6 SRL $5, $25, 13 NOR $15, $10, $12 XOR $10, $11, $9 SLTU $26, $5, $13 ADDIU $31, $0, -32768
  //   ANDI $13, $14, 59109 XOR $31, $4, $9 SLTIU $6, $17, 13013 SLTIU $0, $15, 13356 XORI $27, $6, 53881
  //   SLT $13, $29, $27 XOR $28, $13, $11 ADDIU $31, $0, 32767 NOR $14, $31, $11 XORI $25, $8, 52532 ANDI
  //   $10, $10, 41196 SLTIU $6, $4, 6535 SLTI $1, $12, -5262 SRLV $5, $1, $11 ADDIU $5, $19, -969 ADDIU
  //   $31, $31, 32767 LUI $13, 25703 SUBU $25, $6, $15 SRLV $23, $8, $9 SRA $21, $26, 31 ADDIU $31, $31,
  //   -32768 ORI $29, $0, 23738 XORI $8, $7, 19741 AND $15, $11, $7 SRLV $13, $28, $12 ADDU $7, $22, $23
  //   OR $16, $25, $11 ORI $24, $8, 62638 SLTIU $0, $0, -32768 MOVN $18, $30, $22 MOVZ $3, $13, $4 AND
  //   $18, $21, $6 OR $1, $10, $30 SLTIU $0, $0, 32767 SLTIU $25, $30, 9406 XOR $29, $2, $2 SLL $18, $6,
  //   11 SLTIU $0, $31, -32768 XORI $5, $7, 20248 SLLV $11, $9, $15 AND $20, $6, $29 SRA $26, $27, 9 SLTU
  //   $25, $22, $7 SLT $20, $10, $8 XORI $12, $15, 41185 SLTIU $0, $31, 32767 NOR $11, $20, $31 MOVZ $1,
  //   $28, $20 ADDU $23, $20, $10 ADDU $27, $1, $25 SRLV $4, $1, $1 SRL $3, $6, 30 SLTIU $31, $0, -32768
  //   SLTU $22, $13, $16 SRAV $3, $31, $13 AND $5, $17, $22 XOR $28, $14, $21 ORI $22, $13, 15462 SRAV $2,
  //   $5, $16 SLTIU $31, $0, 32767 ADDIU $9, $21, 22147 SLL $14, $12, 14 NOR $15, $22, $15 SRLV $22, $2,
  //   $10 SLTIU $31, $0, 32767 NOR $14, $6, $5 SLT $3, $4, $25 SLL $14, $0, 0 SLTIU $4, $10, 29433 XOR $0,
  //   $7, $27 MOVN $6, $9, $20 SLTIU $31, $31, 32767 SRA $27, $18, 4 AND $15, $25, $21 NOR $0, $30, $31
  //   MOVZ $19, $27, $1 OR $3, $0, $11 SUBU $26, $0, $24 SLT $30, $24, $25 ORI $13, $1, 18818 MOVN $23,
  //   $19, $29 SLTIU $31, $31, 32767 ANDI $3, $21, 10078 MOVN $1, $6, $6 SRA $24, $21, 16 SRA $6, $9, 20
  //   XOR $8, $5, $30 SLLV $19, $27, $30 SLTIU $31, $31, 32767 SLT $23, $6, $5 OR $1, $9, $22 SRL $13,
  //   $12, 7 LUI $12, 64323 AND $3, $19, $4 SRA $11, $3, 5 LUI $17, 3214 SRAV $27, $28, $0 SLTIU $31, $31,
  //   -32768 LUI $9, 59079 SRLV $5, $23, $23 MOVZ $12, $18, $10 SLL $31, $20, 11 ORI $17, $11, 64442 SLTI
  //   $0, $0, -32768 SUBU $11, $12, $6 ORI $14, $27, 58507 SLL $13, $5, 26 SLTI $0, $0, 32767 MOVN $29,
  //   $29, $2 SLT $2, $13, $22 SRL $27, $3, 20 SLTIU $5, $17, 1424 SUBU $10, $11, $6 SLTI $0, $31, -32768
  //   ADDU $23, $9, $27 SLTIU $25, $17, 11183 SLLV $27, $1, $1 SRLV $5, $25, $22 MOVZ $27, $7, $14 SLTI
  //   $0, $31, 32767 MOVN $1, $1, $16 SLTIU $15, $1, 24847 SLTI $10, $10, -25169 SRA $12, $20, 3 SLT $15,
  //   $29, $22 SLTI $31, $0, -32768 ORI $18, $1, 53131 SLTU $6, $10, $21 LUI $26, 11137 SRAV $24, $4, $27
  //   SLTI $23, $29, -25156 SLTI $31, $0, 32767 SLTI $9, $8, 22415 SLLV $27, $3, $22 MOVN $21, $24, $2 SLL
  //   $2, $5, 5 SLT $19, $14, $11 XORI $14, $15, 2823 SRLV $23, $8, $20 SLTI $31, $31, 32767 LUI $29, 792
  //   SRAV $15, $26, $31 SLTU $15, $20, $5 NOR $12, $5, $5 SRA $10, $18, 20 ADDIU $18, $1, 31441 ADDU $10,
  //   $16, $24 ADDIU $11, $14, -9099 SLTI $31, $31, -32768 LUI $10, 51783 SRAV $3, $19, $13 SUBU $20, $8,
  //   $17 LUI $0, 45036 ORI $12, $3, 40358 OR $6, $31, $28 ANDI $0, $0, 0 ORI $0, $15, 25340 XOR $5, $20,
  //   $7 SUBU $23, $31, $0 SLTU $29, $5, $11 SLTIU $10, $21, 23876 ANDI $0, $0, 65535 ADDU $3, $23, $10
  //   SRLV $4, $3, $7 SLLV $12, $15, $15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
endmodule

module control (
  input  [31:0] Inst,
  output [3:0] AluOp,
  output MOVN,
  output Sa,
  output [4:0] Shamt,
  output [4:0] rA,
  output Mux3,
  output [4:0] rB,
  output [4:0] rW,
  output WE,
  output Mux1,
  output Mux2,
  output Mux4,
  output SLTUMux
);

  wire and_1_out, and_2_out, and_3_out, and_4_out, and_5_out, movdetector_1_o, not_1_out, not_2_out,
       not_3_out, not_4_out, not_5_out, not_7_out, not_8_out, not_9_out, not_10_out, we_funct_1_we;
  wire [4:0] not_11_out;

  not not_1 (not_1_out, Inst[4]);
  and and_1 (and_1_out, Inst[5], not_1_out, Inst[3], not_2_out, Inst[1]);
  not not_2 (not_2_out, Inst[2]);
  not not_3 (not_3_out, Inst[31]);
  not not_4 (not_4_out, Inst[30]);
  not not_5 (not_5_out, Inst[28]);
  not not_6 (MOVN, Inst[0]);
  and and_2 (and_2_out, not_3_out, not_4_out, Inst[29], not_5_out, Inst[27]);
  and and_3 (and_3_out, ~Inst[31], ~Inst[30], ~Inst[29], ~Inst[28], ~Inst[27], ~Inst[26]);  // AND_Gate
  WE_Funct we_funct_1 (
    .F0(Inst[5]), .F1(Inst[4]), .F2(Inst[3]), .F3(Inst[2]), .F4(Inst[1]), .F5(Inst[0]), .WE(we_funct_1_we));
  WE_Opcode we_opcode_1 (
    .O0(Inst[31]), .O1(Inst[30]), .O2(Inst[29]), .O3(Inst[28]), .O4(Inst[27]), .O5(Inst[26]), .WE(Mux1));
  Multiplexer #(.enable("false")) multiplexer_1 (.in0(Inst[26]), .in1(Inst[0]), .out(SLTUMux), .sel(and_3_out));
  Multiplexer #(.enable("false")) multiplexer_2 (.in0(and_2_out), .in1(and_1_out), .out(Mux2), .sel(and_3_out));
  Multiplexer #(.enable("false")) multiplexer_3 (.in0(Mux1), .in1(we_funct_1_we), .out(WE), .sel(and_3_out));
  not not_7 (not_7_out, Inst[5]);
  not not_8 (not_8_out, Inst[4]);
  not not_9 (not_9_out, Inst[2]);
  not not_10 (not_10_out, Inst[2]);
  and and_4 (and_4_out, not_7_out, not_8_out, Inst[3], not_9_out);
  and and_5 (and_5_out, Inst[27], Inst[26], Inst[28], Inst[29], ~Inst[31], ~Inst[30]);  // AND_Gate
  or or_1 (Sa, and_5_out, not_10_out);
  and and_6 (Mux3, and_4_out, and_3_out);
  MOVDetector movdetector_1 (
    .i5(Inst[5]), .i4(Inst[4]), .i3(Inst[3]), .i2(Inst[2]), .i1(Inst[1]), .i0(Inst[0]), .O(movdetector_1_o));
  assign not_11_out = ~{Inst[31], Inst[29:28], Inst[26], Inst[27]};  // NOT_Gate not_11, 5 bits wide
  OpConverter opconverter_1 (.Op6(Inst[31:26]), .funct(Inst[5:0]), .op4(AluOp));
  Multiplexer #(.width(5), .enable("false")) multiplexer_4 (.in0(Inst[15:11]), .in1(Inst[20:16]), .out(rW), .sel(Mux1));
  Multiplexer #(.width(5), .enable("false")) multiplexer_5 (
    .in0(Inst[25:21]), .in1(Inst[20:16]), .out(rA), .sel(movdetector_1_o));
  Multiplexer #(.width(5), .enable("false")) multiplexer_6 (
    .in0(Inst[20:16]), .in1(Inst[25:21]), .out(rB), .sel(movdetector_1_o));
  Multiplexer #(.width(5), .enable("false")) multiplexer_7 (
    .in0(Inst[10:6]), .in1(not_11_out), .out(Shamt), .sel(and_5_out));

  assign Mux4 = Inst[28];
endmodule

module WE_Opcode (
  input  O0,
  input  O1,
  input  O2,
  input  O3,
  input  O4,
  input  O5,
  output WE
);

  wire and_1_out, and_2_out, and_3_out, not_1_out, not_2_out, not_3_out, not_4_out, not_5_out, not_6_out;

  not not_1 (not_1_out, O0);
  not not_2 (not_2_out, O1);
  not not_3 (not_3_out, O0);
  not not_4 (not_4_out, O1);
  not not_5 (not_5_out, O0);
  not not_6 (not_6_out, O1);
  and and_1 (and_1_out, not_1_out, not_2_out, O2, O5);
  and and_2 (and_2_out, not_3_out, not_4_out, O2, O4);
  and and_3 (and_3_out, not_5_out, not_6_out, O2, O3);
  or or_1 (WE, and_1_out, and_2_out, and_3_out);
endmodule

module WE_Funct (
  input  F0,
  input  F1,
  input  F2,
  input  F3,
  input  F4,
  input  F5,
  output WE
);

  wire and_1_out, and_2_out, and_3_out, and_4_out, and_5_out, not_1_out, not_2_out, not_3_out, not_4_out,
       not_5_out, not_6_out, not_7_out, not_8_out, not_9_out, not_10_out, not_11_out, not_12_out, not_13_out,
       not_14_out;

  not not_1 (not_1_out, F0);
  not not_2 (not_2_out, F1);
  not not_3 (not_3_out, F2);
  not not_4 (not_4_out, F5);
  not not_5 (not_5_out, F0);
  not not_6 (not_6_out, F1);
  not not_7 (not_7_out, F2);
  not not_8 (not_8_out, F1);
  not not_9 (not_9_out, F2);
  not not_10 (not_10_out, F5);
  not not_11 (not_11_out, F1);
  not not_12 (not_12_out, F3);
  not not_13 (not_13_out, F1);
  not not_14 (not_14_out, F2);
  and and_1 (and_1_out, not_1_out, not_2_out, not_3_out, not_4_out);
  and and_2 (and_2_out, not_5_out, not_6_out, not_7_out, F4);
  and and_3 (and_3_out, not_8_out, not_9_out, F3, not_10_out);
  and and_4 (and_4_out, not_11_out, F2, not_12_out, F4);
  and and_5 (and_5_out, F0, not_13_out, not_14_out, F5);
  or or_1 (WE, and_1_out, and_2_out, and_3_out, and_4_out, and_5_out);
endmodule

module OpConverter (
  input  [5:0] Op6,
  input  [5:0] funct,
  output [3:0] op4
);

  wire and_1_out, and_2_out, and_3_out, and_4_out, and_5_out, and_6_out, and_7_out, and_8_out, not_2_out,
       not_3_out, not_4_out, not_5_out, not_6_out, not_7_out, not_8_out;
  wire [5:0] multiplexer_1_out, not_1_out;

  assign not_1_out = ~Op6;  // NOT_Gate not_1, 6 bits wide
  and and_1 (and_1_out, not_1_out[0], not_1_out[1], not_1_out[2], not_1_out[3], not_1_out[4], not_1_out[5]);
  Multiplexer #(.width(6), .enable("false")) multiplexer_1 (
    .in0(Op6), .in1(funct), .out(multiplexer_1_out), .sel(and_1_out));
  not not_2 (not_2_out, multiplexer_1_out[1]);
  not not_3 (not_3_out, multiplexer_1_out[0]);
  not not_4 (not_4_out, multiplexer_1_out[3]);
  not not_5 (not_5_out, multiplexer_1_out[0]);
  not not_6 (not_6_out, multiplexer_1_out[1]);
  not not_7 (not_7_out, multiplexer_1_out[5]);
  not not_8 (not_8_out, multiplexer_1_out[3]);
  and and_2 (and_2_out, multiplexer_1_out[3], multiplexer_1_out[2], not_2_out);
  and and_3 (and_3_out, multiplexer_1_out[3], multiplexer_1_out[2], not_3_out);
  and and_4 (and_4_out, multiplexer_1_out[5], multiplexer_1_out[2]);
  and and_5 (and_5_out, not_4_out, multiplexer_1_out[1]);
  and and_6 (and_6_out, multiplexer_1_out[2], multiplexer_1_out[1], not_5_out);
  and and_7 (and_7_out, not_6_out, multiplexer_1_out[0]);
  and and_8 (and_8_out, multiplexer_1_out[5], multiplexer_1_out[0]);
  and and_9 (op4[0], not_7_out, not_8_out, multiplexer_1_out[0]);
  or or_1 (op4[3], and_2_out, and_3_out, and_4_out);
  or or_2 (op4[2], and_5_out, and_6_out);
  or or_3 (op4[1], and_7_out, and_8_out);
endmodule

module MOVDetector (
  input  i5,
  input  i4,
  input  i3,
  input  i2,
  input  i1,
  input  i0,
  output O
);

  wire not_1_out, not_2_out, not_3_out, not_4_out, not_5_out, not_6_out, not_7_out;

  not not_1 (not_1_out, i5);
  not not_2 (not_2_out, i4);
  not not_3 (not_3_out, i2);
  not not_4 (not_4_out, i0);
  not not_5 (not_5_out, i5);
  not not_6 (not_6_out, i3);
  not not_7 (not_7_out, i2);
  and and_1 (O, not_1_out, not_2_out, i3, not_3_out, i1, i1);
  // AND_Gate and_2 has open pins: in0=not_5_out, in1=i4, in2=not_6_out, in3=not_7_out, in4=i1, in5=i0, out=open
endmodule

module Forwarding (
  input  [4:0] IDEXRb,
  input  [4:0] EXMEMrA,
  input  [4:0] EXMEMrW,
  input  [4:0] EXMEMrB,
  input  [4:0] IDEXRa,
  input  [4:0] MEMWBrW,
  input  [4:0] IDEXrW,
  input  EXMEMWE,
  input  IDEXWE,
  input  MEMWBWE,
  input  [4:0] MEMWBrA,
  input  [4:0] MEMWBrB,
  output [1:0] ForwardA,
  output [1:0] ForwardB
);

  wire nor_1_out, nor_2_out, nor_3_out, nor_4_out, or_1_out, or_2_out;
  wire [4:0] xor_1_out, xor_2_out, xor_3_out, xor_4_out;

  or or_1 (or_1_out, EXMEMrW[0], EXMEMrW[1], EXMEMrW[2], EXMEMrW[3], EXMEMrW[4]);
  or or_2 (or_2_out, MEMWBrW[0], MEMWBrW[1], MEMWBrW[2], MEMWBrW[3], MEMWBrW[4]);
  assign xor_1_out = IDEXRb ^ MEMWBrW;  // XOR_Gate xor_1, 5 bits wide
  assign xor_2_out = MEMWBrW ^ IDEXRa;  // XOR_Gate xor_2, 5 bits wide
  assign xor_3_out = IDEXRb ^ EXMEMrW;  // XOR_Gate xor_3, 5 bits wide
  assign xor_4_out = EXMEMrW ^ IDEXRa;  // XOR_Gate xor_4, 5 bits wide
  nor nor_1 (nor_1_out, xor_3_out[0], xor_3_out[1], xor_3_out[2], xor_3_out[3], xor_3_out[4]);
  nor nor_2 (nor_2_out, xor_2_out[0], xor_2_out[1], xor_2_out[2], xor_2_out[3], xor_2_out[4]);
  nor nor_3 (nor_3_out, xor_4_out[0], xor_4_out[1], xor_4_out[2], xor_4_out[3], xor_4_out[4]);
  nor nor_4 (nor_4_out, xor_1_out[0], xor_1_out[1], xor_1_out[2], xor_1_out[3], xor_1_out[4]);
  and and_1 (ForwardA[1], EXMEMWE, or_1_out, nor_3_out);
  and and_2 (ForwardB[1], EXMEMWE, or_1_out, nor_1_out);
  and and_3 (ForwardA[0], MEMWBWE, ~ForwardA[1], or_2_out, nor_2_out);  // AND_Gate
  and and_4 (ForwardB[0], MEMWBWE, ~ForwardB[1], or_2_out, nor_4_out);  // AND_Gate

  // Notes on the sheet:
  //   EX Hazard
endmodule
