// Logisim project ALU_template.circ as structural Verilog: 3 circuits, main circuit ALU32
module LeftShift32 (
  input  [31:0] B,
  input  [4:0] Sa,
  input  Cin,
  output [31:0] C
);


  // Notes on the sheet:
  //   Do not delete or rename any of the input or output pins, and do not add any other pins.
  //   (It's fine to move them around, though)
endmodule

module Add32 (
  input  [31:0] A,
  input  [31:0] B,
  input  Cin,
  output [31:0] C,
  output V
);


  // Notes on the sheet:
  //   Do not delete or rename any of the input or output pins, and do not add any other pins.
  //   (It's fine to move the pins around, though)
endmodule

module ALU32 (
  input  [31:0] A,
  input  [31:0] B,
  input  [3:0] Op,
  input  [4:0] Sa,
  output [31:0] C,
  output V
);


  // Notes on the sheet:
  //   Do not delete or rename any of the input or output pins, and do not add any other pins.
  //   (It's fine to move the pins around, though)
endmodule
